// Logisim project P0_L0_CRC.circ as structural Verilog: 2 circuits, main circuit CRC
module CRC (
  input  [7:0] in_1,
  input  [3:0] in_2,
  output [10:0] out_3
);

  wire _0, _1, _2, _3, _4, _5, _6;
  wire [2:0] o1, o2, o3, o4, o5, o6, o7;
  wire [10:0] bit_extender_1_out;
  wire [10:7] shifter_1_out;

  assign bit_extender_1_out = {{3{1'b0}}, in_1};  // Bit_Extender bit_extender_1
  Shifter #(.width(11)) shifter_1 (
    .in(bit_extender_1_out), .\dist (4'b0011), .out({shifter_1_out, _6, _5, _4, _3, _2, _1, _0}));
  // Probe on shifter_1_out
  _4bmod2 u_4bmod2_1 (.in_1(shifter_1_out), .in_2(in_2), .out_3(o1));
  _4bmod2 u_4bmod2_2 (.in_1({o1, _6}), .in_2(in_2), .out_3(o2));
  _4bmod2 u_4bmod2_3 (.in_1({o2, _5}), .in_2(in_2), .out_3(o3));
  _4bmod2 u_4bmod2_4 (.in_1({o3, _4}), .in_2(in_2), .out_3(o4));
  _4bmod2 u_4bmod2_5 (.in_1({o4, _3}), .in_2(in_2), .out_3(o5));
  _4bmod2 u_4bmod2_6 (.in_1({o5, _2}), .in_2(in_2), .out_3(o6));
  _4bmod2 u_4bmod2_7 (.in_1({o6, _1}), .in_2(in_2), .out_3(o7));
  _4bmod2 u_4bmod2_8 (.in_1({o7, _0}), .in_2(in_2), .out_3(out_3[2:0]));
  // Probe on out_3[2:0]

  assign out_3[10:3] = in_1;

  // Other names for the same wires on the sheet: div[3:0] = in_2; o8[2:0] = out_3[2:0]; in[7:0] = in_1
endmodule

module _4bmod2 (
  input  [3:0] in_1,
  input  [3:0] in_2,
  output [2:0] out_3
);

  wire flag;
  wire [3:0] multiplexer_1_out, shifter_1_out, xor_1_out;

  // Probe on shifter_1_out
  Shifter #(.width(4), .shift("lr")) shifter_1 (.in(in_1), .\dist (2'b11), .out(shifter_1_out));
  assign xor_1_out = in_1 ^ in_2;  // XOR_Gate xor_1, 4 bits wide
  // Probe on flag
  Comparator #(.width(4), .mode("unsigned")) comparator_1 (.a(shifter_1_out), .b(4'b0001), .eq(flag));  // open: gt, lt
  Multiplexer #(.width(4)) multiplexer_1 (
    .in0(in_1), .in1(xor_1_out), .out(multiplexer_1_out), .sel(flag));  // open: en
  Bit_Extender #(.in_width(4), .out_width(3)) bit_extender_1 (.in(multiplexer_1_out), .out(out_3));
endmodule
