// Logisim project P0_L0_FSM.circ as structural Verilog: 3 circuits, main circuit fsm
module fsm (
  input  in_1,
  input  [1:0] in_2,
  output out_3
);

  wire clk;
  wire [2:0] move_1_o0, multiplexer_1_out, register_1_q;

  Clock clock_1 (.out(clk));
  move move_1 (
    .s2(register_1_q[2]), .s1(register_1_q[1]), .s0(register_1_q[0]), .i1(in_2[1]), .i0(in_2[0]),
    .o2(move_1_o0[2]), .o1(move_1_o0[1]), .o0(move_1_o0[0]));
  Multiplexer #(.width(3)) multiplexer_1 (
    .in0(move_1_o0), .in1(3'b000), .out(multiplexer_1_out), .sel(in_1));  // open: en
  Register #(.width(3)) register_1 (.D(multiplexer_1_out), .en(1'b1), .Q(register_1_q), .clk(clk));  // open: clr
  out out_1 (.s2(register_1_q[2]), .s1(register_1_q[1]), .s0(register_1_q[0]), .i1(in_2[1]), .i0(in_2[0]), .o(out_3));

  // Other names for the same wires on the sheet: clr = in_1; in[1:0] = in_2
endmodule

module move (
  input  s2,
  input  s1,
  input  s0,
  input  i1,
  input  i0,
  output o2,
  output o1,
  output o0
);

  wire and_1_out, and_3_out, and_4_out, and_5_out, and_6_out, and_7_out, and_8_out, and_9_out, and_10_out,
       and_11_out, and_12_out, and_13_out, and_14_out, and_15_out, and_16_out, and_17_out, and_18_out,
       and_19_out, and_20_out, not_1_out, not_2_out, not_3_out, not_4_out, not_5_out, not_6_out, not_7_out,
       not_8_out, not_9_out, not_10_out, not_11_out, not_12_out, not_13_out, not_14_out, not_15_out,
       not_16_out, not_17_out, or_1_out, or_2_out, or_3_out, or_4_out;

  and and_1 (and_1_out, s1, s0);
  not not_1 (not_1_out, i0);
  not not_2 (not_2_out, s1);
  not not_3 (not_3_out, s1);
  not not_4 (not_4_out, s0);
  not not_5 (not_5_out, s0);
  not not_6 (not_6_out, s1);
  not not_7 (not_7_out, s0);
  not not_8 (not_8_out, i1);
  not not_9 (not_9_out, s1);
  not not_10 (not_10_out, s0);
  not not_11 (not_11_out, i1);
  and and_2 (o2, and_1_out, not_1_out);
  and and_3 (and_3_out, not_2_out, s0);
  not not_12 (not_12_out, i1);
  and and_4 (and_4_out, not_3_out, s0);
  not not_13 (not_13_out, i0);
  and and_5 (and_5_out, s1, not_4_out);
  not not_14 (not_14_out, i1);
  and and_6 (and_6_out, s1, not_5_out);
  not not_15 (not_15_out, i0);
  and and_7 (and_7_out, not_6_out, not_7_out);
  and and_8 (and_8_out, not_8_out, i0);
  and and_9 (and_9_out, not_9_out, s0);
  not not_16 (not_16_out, i0);
  and and_10 (and_10_out, s1, not_10_out);
  not not_17 (not_17_out, i0);
  and and_11 (and_11_out, s1, s0);
  and and_12 (and_12_out, not_11_out, i0);
  and and_13 (and_13_out, and_3_out, not_12_out);
  or or_1 (or_1_out, and_13_out, and_14_out);
  and and_14 (and_14_out, and_4_out, not_13_out);
  and and_15 (and_15_out, and_5_out, not_14_out);
  or or_2 (or_2_out, and_15_out, and_16_out);
  and and_16 (and_16_out, and_6_out, not_15_out);
  and and_17 (and_17_out, and_7_out, and_8_out);
  or or_3 (or_3_out, and_17_out, and_18_out);
  and and_18 (and_18_out, and_9_out, not_16_out);
  and and_19 (and_19_out, and_10_out, not_17_out);
  or or_4 (or_4_out, and_19_out, and_20_out);
  and and_20 (and_20_out, and_11_out, and_12_out);
  or or_5 (o1, or_1_out, or_2_out);
  or or_6 (o0, or_3_out, or_4_out);
endmodule

module out (
  input  s2,
  input  s1,
  input  s0,
  input  i1,
  input  i0,
  output o
);

  wire and_1_out, not_1_out;

  and and_1 (and_1_out, s1, s0);
  not not_1 (not_1_out, i0);
  and and_2 (o, and_1_out, not_1_out);
endmodule
