// Logisim project P0_L0_GRF.circ as structural Verilog: 1 circuit, main circuit grf
module grf (
  input  in_1,
  input  in_2,
  input  in_3,
  input  [4:0] in_4,
  input  [4:0] in_5,
  input  [4:0] in_6,
  input  [31:0] in_7,
  output [31:0] out_8,
  output [31:0] out_9
);

  wire [31:0] i0, i1, i2, i3, i4, i5, i6, i7, i8, i9, i10, i11, i12, i13, i14, i15, i16, i17, i18, i19, i20,
       i21, i22, i23, i24, i25, i26, i27, i28, i29, i30, i31, o0, o1, o2, o3, o4, o5, o6, o7, o8, o9, o10,
       o11, o12, o13, o14, o15, o16, o17, o18, o19, o20, o21, o22, o23, o24, o25, o26, o27, o28, o29, o30,
       o31;

  Clock clock_1 ();  // open: out
  Register #(.width(32)) register_1 (.D(i0), .en(in_3), .Q(o0), .clk(in_1), .clr(1'b1));
  Register #(.width(32)) register_2 (.D(i8), .en(in_3), .Q(o8), .clk(in_1), .clr(in_2));
  Register #(.width(32)) register_3 (.D(i16), .en(in_3), .Q(o16), .clk(in_1), .clr(in_2));
  Register #(.width(32)) register_4 (.D(i24), .en(in_3), .Q(o24), .clk(in_1), .clr(in_2));
  Register #(.width(32)) register_5 (.D(i1), .en(in_3), .Q(o1), .clk(in_1), .clr(in_2));
  Register #(.width(32)) register_6 (.D(i9), .en(in_3), .Q(o9), .clk(in_1), .clr(in_2));
  Register #(.width(32)) register_7 (.D(i17), .en(in_3), .Q(o17), .clk(in_1), .clr(in_2));
  Register #(.width(32)) register_8 (.D(i25), .en(in_3), .Q(o25), .clk(in_1), .clr(in_2));
  Multiplexer #(.select(5), .width(32)) multiplexer_1 (
    .in0(o0), .in1(o1), .in2(o2), .in3(o3), .in4(o4), .in5(o5), .in6(o6), .in7(o7), .in8(o8), .in9(o9),
    .in10(o10), .in11(o11), .in12(o12), .in13(o13), .in14(o14), .in15(o15), .in16(o16), .in17(o17),
    .in18(o18), .in19(o19), .in20(o20), .in21(o21), .in22(o22), .in23(o23), .in24(o24), .in25(o25),
    .in26(o26), .in27(o27), .in28(o28), .in29(o29), .in30(o30), .in31(o31), .out(out_8), .sel(in_4));  // open: en
  Register #(.width(32)) register_9 (.D(i2), .en(in_3), .Q(o2), .clk(in_1), .clr(in_2));
  Register #(.width(32)) register_10 (.D(i10), .en(in_3), .Q(o10), .clk(in_1), .clr(in_2));
  Register #(.width(32)) register_11 (.D(i18), .en(in_3), .Q(o18), .clk(in_1), .clr(in_2));
  Register #(.width(32)) register_12 (.D(i26), .en(in_3), .Q(o26), .clk(in_1), .clr(in_2));
  Register #(.width(32)) register_13 (.D(i3), .en(in_3), .Q(o3), .clk(in_1), .clr(in_2));
  Register #(.width(32)) register_14 (.D(i11), .en(in_3), .Q(o11), .clk(in_1), .clr(in_2));
  Register #(.width(32)) register_15 (.D(i19), .en(in_3), .Q(o19), .clk(in_1), .clr(in_2));
  Register #(.width(32)) register_16 (.D(i27), .en(in_3), .Q(o27), .clk(in_1), .clr(in_2));
  Register #(.width(32)) register_17 (.D(i4), .en(in_3), .Q(o4), .clk(in_1), .clr(in_2));
  Register #(.width(32)) register_18 (.D(i12), .en(in_3), .Q(o12), .clk(in_1), .clr(in_2));
  Register #(.width(32)) register_19 (.D(i20), .en(in_3), .Q(o20), .clk(in_1), .clr(in_2));
  Register #(.width(32)) register_20 (.D(i28), .en(in_3), .Q(o28), .clk(in_1), .clr(in_2));
  Multiplexer #(.select(5), .width(32)) multiplexer_2 (
    .in0(o0), .in1(o1), .in2(o2), .in3(o3), .in4(o4), .in5(o5), .in6(o6), .in7(o7), .in8(o8), .in9(o9),
    .in10(o10), .in11(o11), .in12(o12), .in13(o13), .in14(o14), .in15(o15), .in16(o16), .in17(o17),
    .in18(o18), .in19(o19), .in20(o20), .in21(o21), .in22(o22), .in23(o23), .in24(o24), .in25(o25),
    .in26(o26), .in27(o27), .in28(o28), .in29(o29), .in30(o30), .in31(o31), .out(out_9), .sel(in_5));  // open: en
  Register #(.width(32)) register_21 (.D(i5), .en(in_3), .Q(o5), .clk(in_1), .clr(in_2));
  Register #(.width(32)) register_22 (.D(i13), .en(in_3), .Q(o13), .clk(in_1), .clr(in_2));
  Register #(.width(32)) register_23 (.D(i21), .en(in_3), .Q(o21), .clk(in_1), .clr(in_2));
  Register #(.width(32)) register_24 (.D(i29), .en(in_3), .Q(o29), .clk(in_1), .clr(in_2));
  Demultiplexer #(.select(5), .width(32), .tristate("true")) demultiplexer_1 (
    .out0(i0), .out1(i1), .out2(i2), .out3(i3), .out4(i4), .out5(i5), .out6(i6), .out7(i7), .out8(i8),
    .out9(i9), .out10(i10), .out11(i11), .out12(i12), .out13(i13), .out14(i14), .out15(i15), .out16(i16),
    .out17(i17), .out18(i18), .out19(i19), .out20(i20), .out21(i21), .out22(i22), .out23(i23), .out24(i24),
    .out25(i25), .out26(i26), .out27(i27), .out28(i28), .out29(i29), .out30(i30), .out31(i31), .in(in_7),
    .sel(in_6));  // open: en
  Register #(.width(32)) register_25 (.D(i6), .en(in_3), .Q(o6), .clk(in_1), .clr(in_2));
  Register #(.width(32)) register_26 (.D(i14), .en(in_3), .Q(o14), .clk(in_1), .clr(in_2));
  Register #(.width(32)) register_27 (.D(i22), .en(in_3), .Q(o22), .clk(in_1), .clr(in_2));
  Register #(.width(32)) register_28 (.D(i30), .en(in_3), .Q(o30), .clk(in_1), .clr(in_2));
  Register #(.width(32)) register_29 (.D(i7), .en(in_3), .Q(o7), .clk(in_1), .clr(in_2));
  Register #(.width(32)) register_30 (.D(i15), .en(in_3), .Q(o15), .clk(in_1), .clr(in_2));
  Register #(.width(32)) register_31 (.D(i23), .en(in_3), .Q(o23), .clk(in_1), .clr(in_2));
  Register #(.width(32)) register_32 (.D(i31), .en(in_3), .Q(o31), .clk(in_1), .clr(in_2));

  // Other names for the same wires on the sheet: A1[4:0] = in_4; A2[4:0] = in_5; A3[4:0] = in_6; clk = in_1;
  //   RD1[31:0] = out_8; RD2[31:0] = out_9; res = in_2; WD[31:0] = in_7; WE = in_3
endmodule
