// Logisim project P0_L1_ftoi.circ as structural Verilog: 2 circuits, main circuit ftoi
module ftoi (
  input  [15:0] in_1,
  output [31:0] out_2
);

  wire _0, _10, comparator_1_eq, comparator_2_eq, flag, S;
  wire [4:0] E, p, subtractor_1_out, subtractor_2_out;
  wire [10:0] M;
  wire [31:0] bit_extender_1_out, multiplexer_1_out, multiplexer_2_out, negator_1_out, shifter_1_out,
       shifter_2_out;

  split split_1 (.in_1(in_1), .out_2(S), .out_4(E), .out_3(M));
  Comparator #(.width(5)) comparator_1 (.a(E), .b({5{1'b0}}), .eq(comparator_1_eq));  // open: gt, lt
  Comparator #(.width(5)) comparator_2 (.a(E), .b({5{1'b1}}), .eq(comparator_2_eq));  // open: gt, lt
  assign bit_extender_1_out = {{21{1'b0}}, M};  // Bit_Extender bit_extender_1
  or or_1 (flag, comparator_1_eq, comparator_2_eq);
  Subtractor #(.width(5)) subtractor_1 (.a(p), .b(5'b01010), .out(subtractor_1_out));  // open: bin, bout
  Subtractor #(.width(5)) subtractor_2 (.a(5'b01010), .b(p), .out(subtractor_2_out));  // open: bin, bout
  Shifter #(.width(32)) shifter_1 (.in(bit_extender_1_out), .\dist (subtractor_1_out), .out(shifter_1_out));
  Shifter #(.width(32), .shift("lr")) shifter_2 (
    .in(bit_extender_1_out), .\dist (subtractor_2_out), .out(shifter_2_out));
  Multiplexer #(.width(32)) multiplexer_1 (
    .in0(shifter_1_out), .in1(shifter_2_out), .out(multiplexer_1_out), .sel(_10));  // open: en
  Subtractor #(.width(5)) subtractor_3 (.a(E), .b(5'b01111), .out(p));  // open: bin, bout
  Multiplexer #(.width(32)) multiplexer_2 (
    .in0(multiplexer_1_out), .in1({32{1'b0}}), .out(multiplexer_2_out), .sel(flag));  // open: en
  Comparator #(.width(5)) comparator_3 (.a(p), .b(5'b01010), .lt(_10));  // open: gt, eq
  Comparator #(.width(5)) comparator_4 (.a(p), .b({5{1'b0}}), .lt(_0));  // open: gt, eq
  Negator #(.width(32)) negator_1 (.in(multiplexer_2_out), .out(negator_1_out));
  Multiplexer #(.width(32)) multiplexer_3 (
    .in0(multiplexer_2_out), .in1(negator_1_out), .out(out_2), .sel(S));  // open: en
endmodule

module split (
  input  [15:0] in_1,
  output out_2,
  output [10:0] out_3,
  output [4:0] out_4
);

  wire [9:0] bit_extender_1_out;
  wire [15:0] shifter_1_out, shifter_2_out;

  Shifter #(.width(16), .shift("lr")) shifter_1 (.in(in_1), .\dist (4'b1111), .out(shifter_1_out));
  Bit_Extender #(.in_width(16), .out_width(10)) bit_extender_1 (.in(in_1), .out(bit_extender_1_out));
  Shifter #(.width(16), .shift("lr")) shifter_2 (.in(in_1), .\dist (4'b1010), .out(shifter_2_out));
  Bit_Extender #(.in_width(16), .out_width(1)) bit_extender_2 (.in(shifter_1_out), .out(out_2));
  assign out_3 = {{1{1'b1}}, bit_extender_1_out};  // Bit_Extender bit_extender_3
  Bit_Extender #(.in_width(16), .out_width(5)) bit_extender_4 (.in(shifter_2_out), .out(out_4));
endmodule
