// Logisim project P0_L1_navigation.circ as structural Verilog: 4 circuits, main circuit navigation
module navigation (
  input  [1:0] in_1,
  input  in_2,
  input  in_3,
  output out_4,
  output out_5
);

  wire moveh_1_out;
  wire [2:0] moves_1_o0, status;

  moveh moveh_1 (.s2(status[2]), .s1(status[1]), .s0(status[0]), .i1(in_1[1]), .i0(in_1[0]), .out(moveh_1_out));
  moves moves_1 (
    .s2(status[2]), .s1(status[1]), .s0(status[0]), .i1(in_1[1]), .i0(in_1[0]), .o2(moves_1_o0[2]),
    .o1(moves_1_o0[1]), .o0(moves_1_o0[0]));
  Clock clock_1 ();  // open: out
  Register #(.width(1)) register_1 (.D(moveh_1_out), .Q(out_4), .clk(in_2), .clr(in_3));  // open: en
  Register #(.width(3)) register_2 (.D(moves_1_o0), .Q(status), .clk(in_2), .clr(in_3));  // open: en
  outs outs_1 (.s2(status[2]), .s1(status[1]), .s0(status[0]), .out(out_5));

  // Other names for the same wires on the sheet: clk = in_2; in[1:0] = in_1; res = in_3
endmodule

module moves (
  input  s2,
  input  s1,
  input  s0,
  input  i1,
  input  i0,
  output o2,
  output o1,
  output o0
);

  wire and_1_out, and_2_out, and_3_out, and_4_out, and_5_out, and_6_out, and_7_out, and_8_out, and_9_out,
       and_10_out, and_11_out, and_12_out, and_13_out, and_14_out, and_15_out, and_16_out, and_17_out,
       and_18_out, and_19_out, and_20_out, and_21_out, and_22_out, and_23_out, and_24_out, and_25_out,
       and_26_out, and_27_out, and_28_out, not_1_out, not_2_out, not_3_out, not_4_out, not_5_out, not_6_out,
       not_7_out, not_8_out, not_9_out, not_10_out, not_11_out, not_12_out, not_13_out, not_14_out,
       not_15_out, not_16_out, not_17_out, or_2_out, or_3_out, or_4_out, or_5_out, or_6_out;

  not not_1 (not_1_out, s0);
  not not_2 (not_2_out, i1);
  not not_3 (not_3_out, i0);
  not not_4 (not_4_out, i1);
  not not_5 (not_5_out, s1);
  not not_6 (not_6_out, i1);
  not not_7 (not_7_out, s2);
  not not_8 (not_8_out, s1);
  not not_9 (not_9_out, i1);
  not not_10 (not_10_out, i0);
  and and_1 (and_1_out, s1, not_1_out);
  and and_2 (and_2_out, not_2_out, not_3_out);
  and and_3 (and_3_out, s1, s0);
  and and_4 (and_4_out, not_4_out, i0);
  and and_5 (and_5_out, not_5_out, s0);
  not not_11 (not_11_out, i1);
  and and_6 (and_6_out, s0, not_6_out);
  not not_12 (not_12_out, i0);
  not not_13 (not_13_out, s0);
  not not_14 (not_14_out, i1);
  not not_15 (not_15_out, s0);
  not not_16 (not_16_out, i0);
  and and_7 (and_7_out, not_7_out, not_8_out);
  and and_8 (and_8_out, not_9_out, not_10_out);
  and and_9 (and_9_out, s0, i1);
  and and_10 (and_10_out, s1, i1);
  and and_11 (and_11_out, s1, s0);
  not not_17 (not_17_out, i0);
  and and_12 (and_12_out, and_1_out, and_2_out);
  or or_1 (o2, and_12_out, and_13_out);
  and and_13 (and_13_out, and_3_out, and_4_out);
  and and_14 (and_14_out, and_5_out, not_11_out);
  or or_2 (or_2_out, and_14_out, and_15_out);
  and and_15 (and_15_out, and_6_out, not_12_out);
  and and_16 (and_16_out, s1, not_13_out);
  and and_17 (and_17_out, and_16_out, and_18_out);
  and and_18 (and_18_out, not_14_out, i0);
  and and_19 (and_19_out, s1, not_15_out);
  and and_20 (and_20_out, and_19_out, and_21_out);
  and and_21 (and_21_out, i1, not_16_out);
  and and_22 (and_22_out, s1, s0);
  and and_23 (and_23_out, and_22_out, and_24_out);
  and and_24 (and_24_out, i1, i0);
  and and_25 (and_25_out, and_7_out, and_8_out);
  or or_3 (or_3_out, and_25_out, and_26_out);
  and and_26 (and_26_out, and_9_out, i0);
  and and_27 (and_27_out, and_10_out, i0);
  or or_4 (or_4_out, and_27_out, and_28_out);
  and and_28 (and_28_out, and_11_out, not_17_out);
  or or_5 (or_5_out, or_2_out, and_17_out);
  or or_6 (or_6_out, and_20_out, and_23_out);
  or or_7 (o0, or_3_out, or_4_out);
  or or_8 (o1, or_5_out, or_6_out);
endmodule

module outs (
  input  s2,
  input  s1,
  input  s0,
  output out
);


  assign out = s2;
endmodule

module moveh (
  input  s2,
  input  s1,
  input  s0,
  input  i1,
  input  i0,
  output out
);

  wire and_1_out, and_2_out, and_3_out, and_4_out, and_5_out, and_6_out, and_7_out, and_8_out, and_9_out,
       and_10_out, and_11_out, and_12_out, and_13_out, and_14_out, not_1_out, not_2_out, not_3_out,
       not_4_out, not_5_out, not_6_out, not_7_out, not_8_out, not_9_out, not_10_out, not_11_out, or_1_out,
       or_2_out, or_3_out;

  not not_1 (not_1_out, s2);
  not not_2 (not_2_out, s0);
  not not_3 (not_3_out, i1);
  not not_4 (not_4_out, s2);
  not not_5 (not_5_out, s1);
  not not_6 (not_6_out, s0);
  and and_1 (and_1_out, not_1_out, not_2_out);
  and and_2 (and_2_out, not_3_out, i0);
  and and_3 (and_3_out, not_4_out, not_5_out);
  and and_4 (and_4_out, not_6_out, i1);
  not not_7 (not_7_out, s2);
  not not_8 (not_8_out, s0);
  not not_9 (not_9_out, i0);
  not not_10 (not_10_out, i1);
  not not_11 (not_11_out, i0);
  and and_5 (and_5_out, and_1_out, and_2_out);
  or or_1 (or_1_out, and_5_out, and_6_out);
  and and_6 (and_6_out, and_3_out, and_4_out);
  and and_7 (and_7_out, not_7_out, not_8_out);
  and and_8 (and_8_out, and_7_out, and_9_out);
  and and_9 (and_9_out, i1, not_9_out);
  and and_10 (and_10_out, s0, i1);
  and and_11 (and_11_out, and_10_out, i0);
  and and_12 (and_12_out, s1, s0);
  and and_13 (and_13_out, and_12_out, and_14_out);
  and and_14 (and_14_out, not_10_out, not_11_out);
  or or_2 (or_2_out, or_1_out, and_8_out);
  or or_3 (or_3_out, and_11_out, and_13_out);
  or or_4 (out, or_2_out, or_3_out);
endmodule
