// Logisim project cpu.circ as structural Verilog: 11 circuits, main circuit main
module main (
  input  in_1,
  output [31:0] out_2,
  output out_3,
  output [4:0] out_4,
  output [31:0] out_5,
  output out_6,
  output [4:0] out_7,
  output [31:0] out_8
);

  wire ALUBSel, clk, clock_2_out, clock_3_out, clock_4_out, equal, EXTop, undriven;
  wire [1:0] A3Sel, DMWop, jumpop, RWDSel;
  wire [2:0] DMRop;
  wire [3:0] ALUop;
  wire [4:0] Rd, Rs, Rt, shamt;
  wire [5:0] funct, opcode;
  wire [15:0] imm16;
  wire [25:0] imm26;
  wire [31:0] ALUout, DMout, DMtemp, EXTout, ifu_1_pc, multiplexer_3_out, npc_1_out_6, PC_4, RD1, RD2;

  Clock clock_1 (.out(clk));
  NPC npc_1 (.in_1(ifu_1_pc), .in_3(imm26), .in_4(jumpop), .in_5(equal), .out_6(npc_1_out_6), .out_7(PC_4), .in_2(RD1));
  IFU ifu_1 (.instruction(out_2), .reset(in_1), .NPC(npc_1_out_6), .clk(clock_2_out), .PC(ifu_1_pc));
  Clock clock_2 (.out(clock_2_out));
  SPLIT split_1 (
    .in_1(out_2), .out_2(opcode), .out_3(Rs), .out_4(Rt), .out_5(Rd), .out_6(shamt), .out_7(funct),
    .out_8(imm16), .out_9(imm26));
  CU cu_1 (
    .in_1(opcode), .in_2(funct), .out_3(out_3), .out_4(A3Sel), .out_5(out_6), .out_7(ALUop), .out_6(RWDSel),
    .out_8(ALUBSel), .out_9(EXTop), .out_10(jumpop), .out_11(DMRop), .out_12(DMWop));
  Multiplexer #(.select(2), .width(5)) multiplexer_1 (
    .in0(Rt), .in1(Rd), .in2({5{1'b1}}), .out(out_4), .sel(A3Sel));  // open: in3, en
  Multiplexer #(.select(2), .width(32)) multiplexer_2 (
    .in0({ALUout[31:7], out_7, ALUout[1:0]}), .in1(DMout), .in2(PC_4), .out(out_5), .sel(RWDSel));  // open: in3, en
  Clock clock_3 (.out(clock_3_out));
  GRF grf_1 (
    .in_2(in_1), .in_3(out_3), .in_4(Rs), .in_5(Rt), .in_6(out_4), .in_7(out_5), .out_8(RD1), .out_9(RD2),
    .in_1(clock_3_out));
  Multiplexer #(.width(32)) multiplexer_3 (
    .in0(RD2), .in1(EXTout), .out(multiplexer_3_out), .sel(ALUBSel));  // open: en
  // Probe on undriven
  ALU alu_1 (
    .in_1(RD1), .in_2(ALUop), .in_3(multiplexer_3_out), .out_5(equal),
    .out_6({ALUout[31:7], out_7, ALUout[1:0]}), .in_4(shamt));
  EXT ext_1 (.EXTin(imm16), .EXTop(EXTop), .EXTout(EXTout));
  DMW dmw_1 (.in_1({ALUout[31:7], out_7, ALUout[1:0]}), .in_2(DMtemp), .in_3(RD2), .in_4(DMWop), .out_5(out_8));
  DM dm_1 (.Addr(out_7), .Wdata(out_8), .WE(out_6), .clk(clock_4_out), .reset(in_1), .Rdata(DMtemp));
  Clock clock_4 (.out(clock_4_out));
  DMR dmr_1 (.in_1(DMtemp), .in_2(DMRop), .in_3({ALUout[31:7], out_7, ALUout[1:0]}), .out_4(DMout));

  // Other names for the same wires on the sheet: ALUout[6:2] = out_7; MemAddr[4:0] = out_7; Instr[31:0] = out_2;
  //   MemData[31:0] = out_8; MemWrite = out_6; RegAddr[4:0] = out_4; RegData[31:0] = out_5; RegWrite = out_3;
  //   reset = in_1
endmodule

module CU (
  input  [5:0] in_1,
  input  [5:0] in_2,
  output out_3,
  output [1:0] out_4,
  output out_5,
  output [1:0] out_6,
  output [3:0] out_7,
  output out_8,
  output out_9,
  output [1:0] out_10,
  output [2:0] out_11,
  output [1:0] out_12
);

  wire addi, addu, \and , beq, comparator_2_eq, comparator_3_eq, comparator_4_eq, comparator_5_eq,
       comparator_6_eq, comparator_7_eq, comparator_8_eq, comparator_9_eq, j, jal, jr, lb, lh, lui, lw, \or ,
       or_1_out, or_2_out, or_3_out, or_4_out, or_5_out, or_6_out, or_7_out, or_8_out, or_9_out, or_10_out,
       or_11_out, ori, R, sb, sh, sll, sllv, slt, subu, sw;

  Comparator #(.width(6)) comparator_1 (.a(in_1), .b({6{1'b0}}), .eq(R));  // open: gt, lt
  Comparator #(.width(6)) comparator_2 (.a(in_2), .b(6'b100000), .eq(comparator_2_eq));  // open: gt, lt
  Comparator #(.width(6)) comparator_3 (.a(in_2), .b(6'b100010), .eq(comparator_3_eq));  // open: gt, lt
  Comparator #(.width(6)) comparator_4 (.a(in_2), .b(6'b100100), .eq(comparator_4_eq));  // open: gt, lt
  Comparator #(.width(6)) comparator_5 (.a(in_2), .b(6'b100101), .eq(comparator_5_eq));  // open: gt, lt
  Comparator #(.width(6)) comparator_6 (.a(in_2), .b(6'b001000), .eq(comparator_6_eq));  // open: gt, lt
  Comparator #(.width(6)) comparator_7 (.a(in_2), .b({6{1'b0}}), .eq(comparator_7_eq));  // open: gt, lt
  Comparator #(.width(6)) comparator_8 (.a(in_2), .b(6'b000100), .eq(comparator_8_eq));  // open: gt, lt
  Comparator #(.width(6)) comparator_9 (.a(in_2), .b(6'b101010), .eq(comparator_9_eq));  // open: gt, lt
  and and_1 (addu, comparator_2_eq, R);
  and and_2 (subu, comparator_3_eq, R);
  and and_3 (\and , comparator_4_eq, R);
  and and_4 (\or , comparator_5_eq, R);
  and and_5 (jr, comparator_6_eq, R);
  and and_6 (sll, comparator_7_eq, R);
  and and_7 (sllv, comparator_8_eq, R);
  and and_8 (slt, comparator_9_eq, R);
  Comparator #(.width(6)) comparator_10 (.a(in_1), .b(6'b100011), .eq(lw));  // open: gt, lt
  Comparator #(.width(6)) comparator_11 (.a(in_1), .b(6'b101011), .eq(sw));  // open: gt, lt
  Comparator #(.width(6)) comparator_12 (.a(in_1), .b(6'b001111), .eq(lui));  // open: gt, lt
  Comparator #(.width(6)) comparator_13 (.a(in_1), .b(6'b001101), .eq(ori));  // open: gt, lt
  Comparator #(.width(6)) comparator_14 (.a(in_1), .b(6'b001000), .eq(addi));  // open: gt, lt
  Comparator #(.width(6)) comparator_15 (.a(in_1), .b(6'b100001), .eq(lh));  // open: gt, lt
  Comparator #(.width(6)) comparator_16 (.a(in_1), .b(6'b100000), .eq(lb));  // open: gt, lt
  or or_1 (or_1_out, subu, beq);
  or or_2 (or_2_out, ori, \or );
  buf or_3 (or_3_out, \and );  // OR_Gate
  or or_4 (or_4_out, addu, lw, sw, addi);
  Comparator #(.width(6)) comparator_17 (.a(in_1), .b(6'b101001), .eq(sh));  // open: gt, lt
  Comparator #(.width(6)) comparator_18 (.a(in_1), .b(6'b101000), .eq(sb));  // open: gt, lt
  or or_5 (or_5_out, R, lui, ori);
  or or_6 (or_6_out, j, jal);
  or or_7 (or_7_out, lw, sw, addi, lh, lb, sh, sb);
  Pull_Resistor pull_resistor_1 (.node(out_7));
  Priority_Encoder #(.select(4)) priority_encoder_1 (
    .in0(or_4_out), .in1(or_1_out), .in2(lui), .in3(or_2_out), .in4(or_3_out), .in5(sll), .in6(sllv),
    .in7(slt), .out(out_7));  // open: in8, in9, in10, in11, in12, in13, in14, in15, gs, en_out, en_in
  Pull_Resistor pull_resistor_2 (.node(out_9));
  Priority_Encoder #(.select(1)) priority_encoder_2 (
    .in0(or_5_out), .in1(or_7_out), .out(out_9));  // open: gs, en_out, en_in
  Pull_Resistor pull_resistor_3 (.node(out_10));
  Priority_Encoder #(.select(2)) priority_encoder_3 (
    .in1(beq), .in2(or_6_out), .in3(jr), .out(out_10));  // open: in0, gs, en_out, en_in
  Pull_Resistor pull_resistor_4 (.node(out_11));
  Priority_Encoder priority_encoder_4 (
    .in1(lh), .in2(lb), .out(out_11));  // open: in0, in3, in4, in5, in6, in7, en_in, gs, en_out
  Pull_Resistor pull_resistor_5 (.node(out_12));
  Priority_Encoder #(.select(2)) priority_encoder_5 (
    .in1(sh), .in2(sb), .out(out_12));  // open: in0, in3, gs, en_out, en_in
  Comparator #(.width(6)) comparator_19 (.a(in_1), .b(6'b000100), .eq(beq));  // open: gt, lt
  Comparator #(.width(6)) comparator_20 (.a(in_1), .b(6'b000010), .eq(j));  // open: gt, lt
  Comparator #(.width(6)) comparator_21 (.a(in_1), .b(6'b000011), .eq(jal));  // open: gt, lt
  or or_8 (or_8_out, lw, sw, lui, ori);
  or or_9 (or_9_out, R, lui, ori);
  or or_10 (or_10_out, lw, lh, lb);
  or or_11 (or_11_out, sh, sb, lw, sw, lui, ori, addi, lh, lb);
  Priority_Encoder #(.select(2)) priority_encoder_6 (
    .in0(or_8_out), .in1(R), .in2(jal), .out(out_4));  // open: in3, gs, en_out, en_in
  Priority_Encoder #(.select(2)) priority_encoder_7 (
    .in0(or_9_out), .in1(or_10_out), .in2(jal), .out(out_6));  // open: in3, gs, en_out, en_in
  Priority_Encoder #(.select(1)) priority_encoder_8 (.in0(R), .in1(or_11_out), .out(out_8));  // open: gs, en_out, en_in
  // Probe on out_4
  Pull_Resistor pull_resistor_6 (.node(out_4));
  Pull_Resistor pull_resistor_7 (.node(out_6));
  Pull_Resistor pull_resistor_8 (.node(out_8));
  or or_12 (out_3, addi, addu, subu, lui, ori, lw, jal, \or , \and , sll, sllv, slt, lh, lb);
  or or_13 (out_5, sw, sh, sb);

  // Other names for the same wires on the sheet: A3Sel[1:0] = out_4; ALUBSel = out_8; ALUop[3:0] = out_7;
  //   DMRop[2:0] = out_11; DMWop[1:0] = out_12; EXTop = out_9; funct[5:0] = in_2; jumpop[1:0] = out_10;
  //   MemWrite = out_5; opcode[5:0] = in_1; RegWrite = out_3; RWDSel[1:0] = out_6
endmodule

module IFU (
  input  [31:0] NPC,
  input  clk,
  input  reset,
  output [31:0] instruction,
  output [31:0] PC
);

  Register #(.width(32)) register_1 (.D(NPC), .Q(PC), .clk(clk), .clr(reset));  // open: en
  ROM #(.addrWidth(5), .dataWidth(32)) rom_1 (.addr(PC[6:2]), .data(instruction));  // open: sel

  // Notes on the sheet:
  //   contents of rom_1 (hex, n*v repeats v):
  //   341c0000 341d0000 34013456 210820 8c010004 ac010004 3c027878 411822 3c051234 34040005 0 ac85ffff
  //   8c83ffff 10650001 1000000d 34670404 10e3000b 0 3c087777 3508ffff 80022 34001100 e65020 34080000
  //   34090001 340a0001 10a4020 1109fffe 1000ffff
endmodule

module NPC (
  input  [31:0] in_1,
  input  [31:0] in_2,
  input  [25:0] in_3,
  input  [1:0] in_4,
  input  in_5,
  output [31:0] out_6,
  output [31:0] out_7
);

  wire [31:0] adder_2_out, bit_extender_1_out, multiplexer_1_out, shifter_1_out;

  Adder #(.width(32)) adder_1 (.a(in_1), .b(32'h4), .out(out_7));  // open: cin, cout
  assign bit_extender_1_out = {{16{in_3[15]}}, in_3[15:0]};  // Bit_Extender bit_extender_1
  Shifter #(.width(32)) shifter_1 (.in(bit_extender_1_out), .\dist (5'b00010), .out(shifter_1_out));
  Adder #(.width(32)) adder_2 (.a(out_7), .b(shifter_1_out), .out(adder_2_out));  // open: cin, cout
  Multiplexer #(.width(32)) multiplexer_1 (
    .in0(out_7), .in1(adder_2_out), .out(multiplexer_1_out), .sel(in_5));  // open: en
  Multiplexer #(.select(2), .width(32)) multiplexer_2 (
    .in0(out_7), .in1(multiplexer_1_out), .in2({in_1[31:28], in_3, 2'b00}), .in3(in_2), .out(out_6),
    .sel(in_4));  // open: en

  // Other names for the same wires on the sheet: imm26[25:0] = in_3; equal = in_5; jumpop[1:0] = in_4;
  //   NPC[31:0] = out_6; PC[31:0] = in_1; PC_4[31:0] = out_7; RD1[31:0] = in_2
endmodule

module SPLIT (
  input  [31:0] in_1,
  output [5:0] out_2,
  output [4:0] out_3,
  output [4:0] out_4,
  output [4:0] out_5,
  output [4:0] out_6,
  output [5:0] out_7,
  output [15:0] out_8,
  output [25:0] out_9
);


  assign out_2 = in_1[31:26];
  assign out_3 = in_1[25:21];
  assign out_4 = in_1[20:16];
  assign out_5 = in_1[15:11];
  assign out_6 = in_1[10:6];
  assign out_7 = in_1[5:0];
  assign out_8 = in_1[15:0];
  assign out_9 = in_1[25:0];
endmodule

module GRF (
  input  in_1,
  input  in_2,
  input  in_3,
  input  [4:0] in_4,
  input  [4:0] in_5,
  input  [4:0] in_6,
  input  [31:0] in_7,
  output [31:0] out_8,
  output [31:0] out_9
);

  wire [31:0] i0, i1, i2, i3, i4, i5, i6, i7, i8, i9, i10, i11, i12, i13, i14, i15, i16, i17, i18, i19, i20,
       i21, i22, i23, i24, i25, i26, i27, i28, i29, i30, i31, o0, o1, o2, o3, o4, o5, o6, o7, o8, o9, o10,
       o11, o12, o13, o14, o15, o16, o17, o18, o19, o20, o21, o22, o23, o24, o25, o26, o27, o28, o29, o30,
       o31;

  Clock clock_1 ();  // open: out
  Register #(.width(32)) register_1 (.D(i0), .en(in_3), .Q(o0), .clk(in_1), .clr(1'b1));
  Register #(.width(32)) register_2 (.D(i8), .en(in_3), .Q(o8), .clk(in_1), .clr(in_2));
  Register #(.width(32)) register_3 (.D(i16), .en(in_3), .Q(o16), .clk(in_1), .clr(in_2));
  Register #(.width(32)) register_4 (.D(i24), .en(in_3), .Q(o24), .clk(in_1), .clr(in_2));
  Register #(.width(32)) register_5 (.D(i1), .en(in_3), .Q(o1), .clk(in_1), .clr(in_2));
  Register #(.width(32)) register_6 (.D(i9), .en(in_3), .Q(o9), .clk(in_1), .clr(in_2));
  Register #(.width(32)) register_7 (.D(i17), .en(in_3), .Q(o17), .clk(in_1), .clr(in_2));
  Register #(.width(32)) register_8 (.D(i25), .en(in_3), .Q(o25), .clk(in_1), .clr(in_2));
  Multiplexer #(.select(5), .width(32)) multiplexer_1 (
    .in0(o0), .in1(o1), .in2(o2), .in3(o3), .in4(o4), .in5(o5), .in6(o6), .in7(o7), .in8(o8), .in9(o9),
    .in10(o10), .in11(o11), .in12(o12), .in13(o13), .in14(o14), .in15(o15), .in16(o16), .in17(o17),
    .in18(o18), .in19(o19), .in20(o20), .in21(o21), .in22(o22), .in23(o23), .in24(o24), .in25(o25),
    .in26(o26), .in27(o27), .in28(o28), .in29(o29), .in30(o30), .in31(o31), .out(out_8), .sel(in_4));  // open: en
  Register #(.width(32)) register_9 (.D(i2), .en(in_3), .Q(o2), .clk(in_1), .clr(in_2));
  Register #(.width(32)) register_10 (.D(i10), .en(in_3), .Q(o10), .clk(in_1), .clr(in_2));
  Register #(.width(32)) register_11 (.D(i18), .en(in_3), .Q(o18), .clk(in_1), .clr(in_2));
  Register #(.width(32)) register_12 (.D(i26), .en(in_3), .Q(o26), .clk(in_1), .clr(in_2));
  Register #(.width(32)) register_13 (.D(i3), .en(in_3), .Q(o3), .clk(in_1), .clr(in_2));
  Register #(.width(32)) register_14 (.D(i11), .en(in_3), .Q(o11), .clk(in_1), .clr(in_2));
  Register #(.width(32)) register_15 (.D(i19), .en(in_3), .Q(o19), .clk(in_1), .clr(in_2));
  Register #(.width(32)) register_16 (.D(i27), .en(in_3), .Q(o27), .clk(in_1), .clr(in_2));
  Register #(.width(32)) register_17 (.D(i4), .en(in_3), .Q(o4), .clk(in_1), .clr(in_2));
  Register #(.width(32)) register_18 (.D(i12), .en(in_3), .Q(o12), .clk(in_1), .clr(in_2));
  Register #(.width(32)) register_19 (.D(i20), .en(in_3), .Q(o20), .clk(in_1), .clr(in_2));
  Register #(.width(32)) register_20 (.D(i28), .en(in_3), .Q(o28), .clk(in_1), .clr(in_2));
  Multiplexer #(.select(5), .width(32)) multiplexer_2 (
    .in0(o0), .in1(o1), .in2(o2), .in3(o3), .in4(o4), .in5(o5), .in6(o6), .in7(o7), .in8(o8), .in9(o9),
    .in10(o10), .in11(o11), .in12(o12), .in13(o13), .in14(o14), .in15(o15), .in16(o16), .in17(o17),
    .in18(o18), .in19(o19), .in20(o20), .in21(o21), .in22(o22), .in23(o23), .in24(o24), .in25(o25),
    .in26(o26), .in27(o27), .in28(o28), .in29(o29), .in30(o30), .in31(o31), .out(out_9), .sel(in_5));  // open: en
  Register #(.width(32)) register_21 (.D(i5), .en(in_3), .Q(o5), .clk(in_1), .clr(in_2));
  Register #(.width(32)) register_22 (.D(i13), .en(in_3), .Q(o13), .clk(in_1), .clr(in_2));
  Register #(.width(32)) register_23 (.D(i21), .en(in_3), .Q(o21), .clk(in_1), .clr(in_2));
  Register #(.width(32)) register_24 (.D(i29), .en(in_3), .Q(o29), .clk(in_1), .clr(in_2));
  Demultiplexer #(.select(5), .width(32), .tristate("true")) demultiplexer_1 (
    .out0(i0), .out1(i1), .out2(i2), .out3(i3), .out4(i4), .out5(i5), .out6(i6), .out7(i7), .out8(i8),
    .out9(i9), .out10(i10), .out11(i11), .out12(i12), .out13(i13), .out14(i14), .out15(i15), .out16(i16),
    .out17(i17), .out18(i18), .out19(i19), .out20(i20), .out21(i21), .out22(i22), .out23(i23), .out24(i24),
    .out25(i25), .out26(i26), .out27(i27), .out28(i28), .out29(i29), .out30(i30), .out31(i31), .in(in_7),
    .sel(in_6));  // open: en
  Register #(.width(32)) register_25 (.D(i6), .en(in_3), .Q(o6), .clk(in_1), .clr(in_2));
  Register #(.width(32)) register_26 (.D(i14), .en(in_3), .Q(o14), .clk(in_1), .clr(in_2));
  Register #(.width(32)) register_27 (.D(i22), .en(in_3), .Q(o22), .clk(in_1), .clr(in_2));
  Register #(.width(32)) register_28 (.D(i30), .en(in_3), .Q(o30), .clk(in_1), .clr(in_2));
  Register #(.width(32)) register_29 (.D(i7), .en(in_3), .Q(o7), .clk(in_1), .clr(in_2));
  Register #(.width(32)) register_30 (.D(i15), .en(in_3), .Q(o15), .clk(in_1), .clr(in_2));
  Register #(.width(32)) register_31 (.D(i23), .en(in_3), .Q(o23), .clk(in_1), .clr(in_2));
  Register #(.width(32)) register_32 (.D(i31), .en(in_3), .Q(o31), .clk(in_1), .clr(in_2));

  // Other names for the same wires on the sheet: A1[4:0] = in_4; A2[4:0] = in_5; A3[4:0] = in_6; clk = in_1;
  //   RD1[31:0] = out_8; RD2[31:0] = out_9; res = in_2; WD[31:0] = in_7; WE = in_3
endmodule

module ALU (
  input  [31:0] in_1,
  input  [3:0] in_2,
  input  [31:0] in_3,
  input  [4:0] in_4,
  output out_5,
  output [31:0] out_6
);

  wire comparator_1_lt;
  wire [31:0] adder_1_out, and_1_out, bit_extender_1_out, or_1_out, shifter_1_out, shifter_2_out,
       shifter_3_out, subtractor_1_out;

  Adder #(.width(32)) adder_1 (.a(in_1), .b(in_3), .out(adder_1_out));  // open: cin, cout
  Subtractor #(.width(32)) subtractor_1 (.a(in_1), .b(in_3), .out(subtractor_1_out));  // open: bin, bout
  Shifter #(.width(32)) shifter_1 (.in(in_3), .\dist (5'b10000), .out(shifter_1_out));
  assign or_1_out = in_1 | in_3;  // OR_Gate or_1, 32 bits wide
  assign and_1_out = in_1 & in_3;  // AND_Gate and_1, 32 bits wide
  Shifter #(.width(32)) shifter_2 (.in(in_3), .\dist (in_4), .out(shifter_2_out));
  Shifter #(.width(32)) shifter_3 (.in(in_3), .\dist (in_1[4:0]), .out(shifter_3_out));
  Comparator #(.width(32)) comparator_1 (.a(in_1), .b(in_3), .lt(comparator_1_lt));  // open: gt, eq
  assign bit_extender_1_out = {{31{1'b0}}, comparator_1_lt};  // Bit_Extender bit_extender_1
  Multiplexer #(.select(4), .width(32)) multiplexer_1 (
    .in0(adder_1_out), .in1(subtractor_1_out), .in2(shifter_1_out), .in3(or_1_out), .in4(and_1_out),
    .in5(shifter_2_out), .in6(shifter_3_out), .in7(bit_extender_1_out), .out(out_6), .sel(in_2));  // open: in8, in9, in10, in11, in12, in13, in14, in15, en
  Comparator #(.width(32)) comparator_2 (.a(subtractor_1_out), .b({32{1'b0}}), .eq(out_5));  // open: gt, lt

  // Other names for the same wires on the sheet: A[31:0] = in_1; ALUControl[3:0] = in_2; B[31:0] = in_3;
  //   shamt[4:0] = in_4
endmodule

module EXT (
  input  [15:0] EXTin,
  input  EXTop,
  output [31:0] EXTout
);

  wire [31:0] bit_extender_1_out, bit_extender_2_out;

  assign bit_extender_1_out = {{16{1'b0}}, EXTin};  // Bit_Extender bit_extender_1
  assign bit_extender_2_out = {{16{EXTin[15]}}, EXTin};  // Bit_Extender bit_extender_2
  Multiplexer #(.width(32)) multiplexer_1 (
    .in0(bit_extender_1_out), .in1(bit_extender_2_out), .out(EXTout), .sel(EXTop));  // open: en
endmodule

module DM (
  input  [4:0] Addr,
  input  [31:0] Wdata,
  input  WE,
  input  clk,
  input  reset,
  output [31:0] Rdata
);

  RAM #(.addrWidth(5), .dataWidth(32), .bus("separate")) ram_1 (
    .addr(Addr), .din(Wdata), .data(Rdata), .str(WE), .clk(clk), .clr(reset));  // open: sel, ld
endmodule

module DMR (
  input  [31:0] in_1,
  input  [2:0] in_2,
  input  [31:0] in_3,
  output [31:0] out_4
);

  wire [7:0] multiplexer_2_out;
  wire [15:0] multiplexer_1_out;
  wire [31:0] bit_extender_1_out, bit_extender_2_out;

  Multiplexer #(.width(16)) multiplexer_1 (
    .in0(in_1[15:0]), .in1(in_1[31:16]), .out(multiplexer_1_out), .sel(in_3[1]));  // open: en
  Multiplexer #(.select(2), .width(8)) multiplexer_2 (
    .in0(in_1[7:0]), .in1(in_1[15:8]), .in2(in_1[23:16]), .in3(in_1[31:24]), .out(multiplexer_2_out),
    .sel(in_3[1:0]));  // open: en
  assign bit_extender_1_out = {{16{multiplexer_1_out[15]}}, multiplexer_1_out};  // Bit_Extender bit_extender_1
  assign bit_extender_2_out = {{24{multiplexer_2_out[7]}}, multiplexer_2_out};  // Bit_Extender bit_extender_2
  Multiplexer #(.select(3), .width(32)) multiplexer_3 (
    .in0(in_1), .in1(bit_extender_1_out), .in2(bit_extender_2_out), .out(out_4), .sel(in_2));  // open: in3, in4, in5, in6, in7, en

  // Other names for the same wires on the sheet: addr[31:0] = in_3; DMout[31:0] = out_4; DMRop[2:0] = in_2;
  //   DMtemp[31:0] = in_1
endmodule

module DMW (
  input  [31:0] in_1,
  input  [31:0] in_2,
  input  [31:0] in_3,
  input  [1:0] in_4,
  output [31:0] out_5
);

  wire [31:0] multiplexer_1_out, multiplexer_2_out;

  Multiplexer #(.width(32)) multiplexer_1 (
    .in0({in_2[31:16], in_3[15:0]}), .in1({in_3[15:0], in_2[15:0]}), .out(multiplexer_1_out), .sel(in_1[1]));  // open: en
  Multiplexer #(.select(2), .width(32)) multiplexer_2 (
    .in0({in_2[31:8], in_3[7:0]}), .in1({in_2[31:16], in_3[7:0], in_2[7:0]}),
    .in2({in_2[31:24], in_3[7:0], in_2[15:0]}), .in3({in_3[7:0], in_2[23:0]}), .out(multiplexer_2_out),
    .sel(in_1[1:0]));  // open: en
  Multiplexer #(.select(2), .width(32)) multiplexer_3 (
    .in0(in_3), .in1(multiplexer_1_out), .in2(multiplexer_2_out), .out(out_5), .sel(in_4));  // open: in3, en

  // Other names for the same wires on the sheet: DM1[15:0] = in_2[31:16]; DM10[7:0] = in_2[23:16];
  //   DM11[7:0] = in_2[31:24]; DM0[15:0] = in_2[15:0]; DM00[7:0] = in_2[7:0]; DM01[7:0] = in_2[15:8];
  //   dat16[15:0] = in_3[15:0]; dat32[31:0] = in_3; data8[7:0] = in_3[7:0]; addr[31:0] = in_1; DMW[31:0] = out_5;
  //   DMWop[1:0] = in_4
endmodule
