// Logisim project fib.circ as structural Verilog: 3 circuits, main circuit main
module main (
  input  [2:0] in_1,
  output [3:0] out_2
);

  wire count_1_out_4, not_1_out;
  wire [3:0] adder_1_out, bit_extender_1_out, cal_1_out_4, count_1_out_3;

  assign bit_extender_1_out = {{1{1'b0}}, in_1};  // Bit_Extender bit_extender_1
  Adder #(.width(4)) adder_1 (.a(bit_extender_1_out), .b(4'b0001), .out(adder_1_out));  // open: cin, cout
  // Probe on count_1_out_3
  count count_1 (.in_2(adder_1_out), .out_3(count_1_out_3), .out_4(count_1_out_4), .in_1(1'b0));
  // Probe on count_1_out_4
  Clock clock_1 ();  // open: out
  cal cal_1 (.in_1(count_1_out_3), .in_2(count_1_out_4), .in_3(1'b0), .out_4(cal_1_out_4));
  Multiplexer #(.width(4)) multiplexer_1 (.in0(4'b0000), .in1(cal_1_out_4), .out(out_2), .sel(not_1_out));  // open: en
  not not_1 (not_1_out, count_1_out_4);
endmodule

module cal (
  input  [3:0] in_1,
  input  in_2,
  input  in_3,
  output [3:0] out_4
);

  wire clk, comparator_1_eq, init;
  wire [3:0] adder_1_out, multiplexer_1_out, pre;

  Clock clock_1 (.out(clk));
  not not_1 (init, comparator_1_eq);
  Comparator #(.width(4), .mode("unsigned")) comparator_1 (
    .a(in_1), .b(4'b0000), .eq(comparator_1_eq));  // open: gt, lt
  // Probe on out_4
  // Probe on pre
  Register #(.width(4)) register_1 (.D(multiplexer_1_out), .en(in_2), .Q(pre), .clk(clk), .clr(in_3));
  Multiplexer #(.width(4)) multiplexer_1 (.in0(4'b0001), .in1(out_4), .out(multiplexer_1_out), .sel(init));  // open: en
  Adder #(.width(4)) adder_1 (.a(out_4), .b(pre), .out(adder_1_out));  // open: cin, cout
  // Probe on pre
  Register #(.width(4)) register_2 (.D(adder_1_out), .en(in_2), .Q(out_4), .clk(clk), .clr(in_3));

  // Other names for the same wires on the sheet: cnt[3:0] = in_1; flag = in_2; now[3:0] = out_4; reset = in_3
endmodule

// cnt
module count (
  input  in_1,
  input  [3:0] in_2,
  output [3:0] out_3,
  output out_4
);

  wire clock_1_out;
  wire [3:0] adder_1_out;

  Clock clock_1 (.out(clock_1_out));
  Register #(.width(4)) register_1 (.D(adder_1_out), .en(out_4), .Q(out_3), .clk(clock_1_out), .clr(in_1));
  Adder #(.width(4)) adder_1 (.a(out_3), .b(4'b0001), .out(adder_1_out));  // open: cin, cout
  Comparator #(.width(4), .mode("unsigned")) comparator_1 (.a(out_3), .b(in_2), .lt(out_4));  // open: gt, eq
endmodule
