// Logisim project fib_power.circ as structural Verilog: 10 circuits, main circuit main
module main (
  input  [31:0] in_1,
  output [31:0] out_2
);

  wire and_1_out, clk, low, stop, t;
  wire [31:0] a11, a12, a21, a22, multiplexer_1_out, n, register_1_q, register_2_q, s11, s12, s21, s22,
       \初始化a_1_out_6 , \初始化a_1_out_7 , \初始化a_1_out_8 , \初始化a_1_out_9 , \初始化s_1_out_6 , \初始化s_1_out_7 ,
       \初始化s_1_out_8 , \初始化s_1_out_9 , \矩阵乘法_1_out_10 , \矩阵乘法_1_out_11 , \矩阵乘法_1_out_12 , \矩阵乘法_1_out_13 ,
       \矩阵乘法_2_out_10 , \矩阵乘法_2_out_11 , \矩阵乘法_2_out_12 , \矩阵乘法_2_out_13 ;

  Clock clock_1 (.out(clk));
  Counter #(.width(1), .max('h1), .ongoal("stay")) counter_1 (.Q(t), .clk(clk));  // open: load, D, count, carry, clr
  Multiplexer #(.width(32)) multiplexer_1 (.in0(in_1), .in1(n), .out(multiplexer_1_out), .sel(t));  // open: en
  Register #(.width(32)) register_1 (.D(multiplexer_1_out), .Q(register_1_q), .clk(clk));  // open: en, clr
  \初始化a  \u_初始化a_1  (
    .in_1(t), .in_2(a11), .in_3(a12), .in_4(a21), .in_5(a22), .out_6(\初始化a_1_out_6 ), .out_7(\初始化a_1_out_7 ),
    .out_8(\初始化a_1_out_8 ), .out_9(\初始化a_1_out_9 ));
  \矩阵乘法  \u_矩阵乘法_1  (
    .in_2(\初始化a_1_out_6 ), .in_3(\初始化a_1_out_7 ), .in_4(\初始化a_1_out_8 ), .in_5(\初始化a_1_out_9 ), .in_6(a11),
    .in_7(a12), .in_8(a21), .in_9(a22), .out_10(\矩阵乘法_1_out_10 ), .in_1(t), .out_11(\矩阵乘法_1_out_11 ),
    .out_12(\矩阵乘法_1_out_12 ), .out_13(\矩阵乘法_1_out_13 ));
  Shifter #(.width(32), .shift("lr")) shifter_1 (.in(register_1_q), .\dist (5'b00001), .out(n));
  Bit_Extender #(.in_width(32), .out_width(1)) bit_extender_1 (.in(register_1_q), .out(low));
  Comparator #(.width(32), .mode("unsigned")) comparator_1 (
    .a(register_1_q), .b({32{1'b0}}), .gt(stop));  // open: eq, lt
  rgt rgt_1 (
    .in_1(\矩阵乘法_1_out_10 ), .in_2(\矩阵乘法_1_out_11 ), .in_3(\矩阵乘法_1_out_12 ), .in_4(\矩阵乘法_1_out_13 ),
    .out_8(a11), .out_9(a12), .out_10(a21), .out_11(a22), .in_5(clk), .in_7(1'b1));  // open: in_6
  Register #(.width(32)) register_2 (.D(s12), .Q(register_2_q), .clk(clk), .clr(stop));  // open: en
  Multiplexer #(.width(32)) multiplexer_2 (.in0(register_2_q), .in1({32{1'b0}}), .out(out_2), .sel(stop));  // open: en
  \初始化s  \u_初始化s_1  (
    .in_1(t), .in_2(s11), .in_3(s12), .in_4(s21), .in_5(s22), .out_6(\初始化s_1_out_6 ), .out_7(\初始化s_1_out_7 ),
    .out_8(\初始化s_1_out_8 ), .out_9(\初始化s_1_out_9 ));
  \矩阵乘法  \u_矩阵乘法_2  (
    .in_2(\初始化s_1_out_6 ), .in_3(\初始化s_1_out_7 ), .in_4(\初始化s_1_out_8 ), .in_5(\初始化s_1_out_9 ), .in_6(a11),
    .in_7(a12), .in_8(a21), .in_9(a22), .out_10(\矩阵乘法_2_out_10 ), .in_1(and_1_out), .out_11(\矩阵乘法_2_out_11 ),
    .out_12(\矩阵乘法_2_out_12 ), .out_13(\矩阵乘法_2_out_13 ));
  and and_1 (and_1_out, t, low);
  rgt rgt_2 (
    .in_1(\矩阵乘法_2_out_10 ), .in_2(\矩阵乘法_2_out_11 ), .in_3(\矩阵乘法_2_out_12 ), .in_4(\矩阵乘法_2_out_13 ),
    .out_8(s11), .out_9(s12), .out_10(s21), .out_11(s22), .in_5(clk), .in_7(1'b1));  // open: in_6
endmodule

module cnt (
  input  [31:0] in_1,
  input  in_2,
  output out_3,
  output out_4
);

  wire clk, t;
  wire [31:0] multiplexer_1_out, n, shifter_1_out;

  Clock clock_1 (.out(clk));
  Counter #(.width(1), .max('h1), .ongoal("stay")) counter_1 (
    .Q(t), .clk(clk), .clr(in_2));  // open: load, D, count, carry
  Multiplexer #(.width(32)) multiplexer_1 (
    .in0(in_1), .in1(shifter_1_out), .out(multiplexer_1_out), .sel(t));  // open: en
  Shifter #(.width(32), .shift("lr")) shifter_1 (.in(n), .\dist (5'b00001), .out(shifter_1_out));
  // Probe on n
  Register #(.width(32)) register_1 (.D(multiplexer_1_out), .Q(n), .clk(clk), .clr(in_2));  // open: en
  Bit_Extender #(.in_width(32), .out_width(1)) bit_extender_1 (.in(n), .out(out_3));
  Comparator #(.width(32), .mode("unsigned")) comparator_1 (.a(n), .b({32{1'b0}}), .eq(out_4));  // open: gt, lt

  // Other names for the same wires on the sheet: clr = in_2; input[31:0] = in_1
endmodule

module cal (
  input  in_1,
  input  in_2,
  input  in_3,
  output [31:0] out_4,
  output [31:0] out_5,
  output [31:0] out_6,
  output [31:0] out_7,
  output [31:0] out_8,
  output [31:0] out_9,
  output [31:0] out_10,
  output [31:0] out_11
);

  wire and_1_out, clk, t;
  wire [31:0] \初始化a_1_out_6 , \初始化a_1_out_7 , \初始化a_1_out_8 , \初始化a_1_out_9 , \初始化s_1_out_6 , \初始化s_1_out_7 ,
       \初始化s_1_out_8 , \初始化s_1_out_9 , \矩阵乘法_1_out_10 , \矩阵乘法_1_out_11 , \矩阵乘法_1_out_12 , \矩阵乘法_1_out_13 ,
       \矩阵乘法_2_out_10 , \矩阵乘法_2_out_11 , \矩阵乘法_2_out_12 , \矩阵乘法_2_out_13 ;

  Counter #(.width(1), .max('h1), .ongoal("stay")) counter_1 (
    .Q(t), .clk(clk), .clr(in_2));  // open: load, D, count, carry
  Clock clock_1 (.out(clk));
  \初始化a  \u_初始化a_1  (
    .in_1(t), .in_2(out_4), .in_3(out_5), .in_4(out_6), .in_5(out_7), .out_6(\初始化a_1_out_6 ),
    .out_7(\初始化a_1_out_7 ), .out_8(\初始化a_1_out_8 ), .out_9(\初始化a_1_out_9 ));
  \初始化s  \u_初始化s_1  (
    .in_1(t), .in_2(out_8), .in_3(out_9), .in_4(out_10), .in_5(out_11), .out_6(\初始化s_1_out_6 ),
    .out_7(\初始化s_1_out_7 ), .out_8(\初始化s_1_out_8 ), .out_9(\初始化s_1_out_9 ));
  \矩阵乘法  \u_矩阵乘法_1  (
    .in_2(\初始化a_1_out_6 ), .in_3(\初始化a_1_out_7 ), .in_4(\初始化a_1_out_8 ), .in_5(\初始化a_1_out_9 ), .in_6(out_4),
    .in_7(out_5), .in_8(out_6), .in_9(out_7), .out_10(\矩阵乘法_1_out_10 ), .in_1(t), .out_11(\矩阵乘法_1_out_11 ),
    .out_12(\矩阵乘法_1_out_12 ), .out_13(\矩阵乘法_1_out_13 ));
  \矩阵乘法  \u_矩阵乘法_2  (
    .in_2(\初始化s_1_out_6 ), .in_3(\初始化s_1_out_7 ), .in_4(\初始化s_1_out_8 ), .in_5(\初始化s_1_out_9 ), .in_6(out_4),
    .in_7(out_5), .in_8(out_6), .in_9(out_7), .out_10(\矩阵乘法_2_out_10 ), .in_1(and_1_out),
    .out_11(\矩阵乘法_2_out_11 ), .out_12(\矩阵乘法_2_out_12 ), .out_13(\矩阵乘法_2_out_13 ));
  and and_1 (and_1_out, in_3, t);
  rgt rgt_1 (
    .in_1(\矩阵乘法_1_out_10 ), .in_2(\矩阵乘法_1_out_11 ), .in_3(\矩阵乘法_1_out_12 ), .in_4(\矩阵乘法_1_out_13 ),
    .out_8(out_4), .out_9(out_5), .out_10(out_6), .out_11(out_7), .in_5(clk), .in_6(in_2), .in_7(in_1));
  rgt rgt_2 (
    .in_1(\矩阵乘法_2_out_10 ), .in_2(\矩阵乘法_2_out_11 ), .in_3(\矩阵乘法_2_out_12 ), .in_4(\矩阵乘法_2_out_13 ),
    .out_8(out_8), .out_9(out_9), .out_10(out_10), .out_11(out_11), .in_5(clk), .in_6(in_2), .in_7(in_1));

  // Other names for the same wires on the sheet: a1[31:0] = out_4; a2[31:0] = out_5; a3[31:0] = out_6;
  //   a4[31:0] = out_7; clr = in_2; flag = in_1; low = in_3; s1[31:0] = out_8; s2[31:0] = out_9; s3[31:0] = out_10;
  //   s4[31:0] = out_11
endmodule

// 自乘
module mul_a (
  input  in_1,
  input  [31:0] in_2,
  input  [31:0] in_3,
  input  [31:0] in_4,
  input  [31:0] in_5,
  output [31:0] out_6,
  output [31:0] out_7,
  output [31:0] out_8,
  output [31:0] out_9
);

  wire [31:0] adder_1_out, adder_2_out, adder_3_out, adder_4_out, multiplier_1_cout, multiplier_1_out,
       multiplier_2_out, multiplier_3_cout, multiplier_3_out, multiplier_4_out, multiplier_5_cout,
       multiplier_5_out, multiplier_6_out, multiplier_7_cout, multiplier_7_out, multiplier_8_out;

  Multiplier #(.width(32)) multiplier_1 (
    .a(in_2), .b(in_2), .out(multiplier_1_out), .cout(multiplier_1_cout));  // open: cin
  Adder #(.width(32)) adder_1 (.a(multiplier_1_out), .b(multiplier_2_out), .out(adder_1_out));  // open: cin, cout
  Multiplier #(.width(32)) multiplier_2 (
    .a(in_3), .b(in_4), .out(multiplier_2_out), .cin(multiplier_1_cout));  // open: cout
  Multiplier #(.width(32)) multiplier_3 (
    .a(in_2), .b(in_3), .out(multiplier_3_out), .cout(multiplier_3_cout));  // open: cin
  Adder #(.width(32)) adder_2 (.a(multiplier_3_out), .b(multiplier_4_out), .out(adder_2_out));  // open: cin, cout
  Multiplier #(.width(32)) multiplier_4 (
    .a(in_3), .b(in_5), .out(multiplier_4_out), .cin(multiplier_3_cout));  // open: cout
  Multiplier #(.width(32)) multiplier_5 (
    .a(in_4), .b(in_2), .out(multiplier_5_out), .cout(multiplier_5_cout));  // open: cin
  Adder #(.width(32)) adder_3 (.a(multiplier_5_out), .b(multiplier_6_out), .out(adder_3_out));  // open: cin, cout
  Multiplier #(.width(32)) multiplier_6 (
    .a(in_5), .b(in_4), .out(multiplier_6_out), .cin(multiplier_5_cout));  // open: cout
  Multiplier #(.width(32)) multiplier_7 (
    .a(in_4), .b(in_3), .out(multiplier_7_out), .cout(multiplier_7_cout));  // open: cin
  Adder #(.width(32)) adder_4 (.a(multiplier_7_out), .b(multiplier_8_out), .out(adder_4_out));  // open: cin, cout
  Multiplier #(.width(32)) multiplier_8 (
    .a(in_5), .b(in_5), .out(multiplier_8_out), .cin(multiplier_7_cout));  // open: cout
  Multiplexer #(.width(32)) multiplexer_1 (.in0(32'h1), .in1(adder_1_out), .out(out_6), .sel(in_1));  // open: en
  Multiplexer #(.width(32)) multiplexer_2 (.in0(32'h1), .in1(adder_2_out), .out(out_7), .sel(in_1));  // open: en
  Multiplexer #(.width(32)) multiplexer_3 (.in0(32'h1), .in1(adder_3_out), .out(out_8), .sel(in_1));  // open: en
  Multiplexer #(.width(32)) multiplexer_4 (.in0({32{1'b0}}), .in1(adder_4_out), .out(out_9), .sel(in_1));  // open: en

  // Other names for the same wires on the sheet: a11[31:0] = in_2; a12[31:0] = in_3; a21[31:0] = in_4;
  //   a22[31:0] = in_5; t = in_1
endmodule

// 寄存器
module rgt (
  input  [31:0] in_1,
  input  [31:0] in_2,
  input  [31:0] in_3,
  input  [31:0] in_4,
  input  in_5,
  input  in_6,
  input  in_7,
  output [31:0] out_8,
  output [31:0] out_9,
  output [31:0] out_10,
  output [31:0] out_11
);

  Register #(.width(32)) register_1 (.D(in_1), .en(in_7), .Q(out_8), .clk(in_5), .clr(in_6));
  Register #(.width(32)) register_2 (.D(in_2), .en(in_7), .Q(out_9), .clk(in_5), .clr(in_6));
  Register #(.width(32)) register_3 (.D(in_3), .en(in_7), .Q(out_10), .clk(in_5), .clr(in_6));
  Register #(.width(32)) register_4 (.D(in_4), .en(in_7), .Q(out_11), .clk(in_5), .clr(in_6));

  // Other names for the same wires on the sheet: a11_in[31:0] = in_1; a11_out[31:0] = out_8; a12_in[31:0] = in_2;
  //   a12_out[31:0] = out_9; a21_in[31:0] = in_3; a21_out[31:0] = out_10; a22_in[31:0] = in_4; a22_out[31:0] = out_11;
  //   clk = in_5; clr = in_6; flag = in_7
endmodule

module \矩阵乘法  (
  input  in_1,
  input  [31:0] in_2,
  input  [31:0] in_3,
  input  [31:0] in_4,
  input  [31:0] in_5,
  input  [31:0] in_6,
  input  [31:0] in_7,
  input  [31:0] in_8,
  input  [31:0] in_9,
  output [31:0] out_10,
  output [31:0] out_11,
  output [31:0] out_12,
  output [31:0] out_13
);

  wire [31:0] adder_1_out, adder_2_out, adder_3_out, adder_4_out, multiplier_1_out, multiplier_2_out,
       multiplier_3_out, multiplier_4_out, multiplier_5_out, multiplier_6_out, multiplier_7_out,
       multiplier_8_out;

  Multiplier #(.width(32)) multiplier_1 (.a(in_2), .b(in_6), .out(multiplier_1_out));  // open: cin, cout
  Multiplier #(.width(32)) multiplier_2 (.a(in_3), .b(in_8), .out(multiplier_2_out));  // open: cin, cout
  Multiplier #(.width(32)) multiplier_3 (.a(in_2), .b(in_7), .out(multiplier_3_out));  // open: cin, cout
  Multiplier #(.width(32)) multiplier_4 (.a(in_3), .b(in_9), .out(multiplier_4_out));  // open: cin, cout
  Multiplier #(.width(32)) multiplier_5 (.a(in_4), .b(in_6), .out(multiplier_5_out));  // open: cin, cout
  Multiplier #(.width(32)) multiplier_6 (.a(in_5), .b(in_8), .out(multiplier_6_out));  // open: cin, cout
  Multiplier #(.width(32)) multiplier_7 (.a(in_4), .b(in_7), .out(multiplier_7_out));  // open: cin, cout
  Multiplier #(.width(32)) multiplier_8 (.a(in_5), .b(in_9), .out(multiplier_8_out));  // open: cin, cout
  Adder #(.width(32)) adder_1 (.a(multiplier_1_out), .b(multiplier_2_out), .out(adder_1_out));  // open: cin, cout
  Adder #(.width(32)) adder_2 (.a(multiplier_3_out), .b(multiplier_4_out), .out(adder_2_out));  // open: cin, cout
  Adder #(.width(32)) adder_3 (.a(multiplier_5_out), .b(multiplier_6_out), .out(adder_3_out));  // open: cin, cout
  Adder #(.width(32)) adder_4 (.a(multiplier_7_out), .b(multiplier_8_out), .out(adder_4_out));  // open: cin, cout
  Multiplexer #(.width(32)) multiplexer_1 (.in0(in_2), .in1(adder_1_out), .out(out_10), .sel(in_1));  // open: en
  Multiplexer #(.width(32)) multiplexer_2 (.in0(in_3), .in1(adder_2_out), .out(out_11), .sel(in_1));  // open: en
  Multiplexer #(.width(32)) multiplexer_3 (.in0(in_4), .in1(adder_3_out), .out(out_12), .sel(in_1));  // open: en
  Multiplexer #(.width(32)) multiplexer_4 (.in0(in_5), .in1(adder_4_out), .out(out_13), .sel(in_1));  // open: en

  // Other names for the same wires on the sheet: a11[31:0] = in_2; a12[31:0] = in_3; a21[31:0] = in_4;
  //   a22[31:0] = in_5; b11[31:0] = in_6; b12[31:0] = in_7; b21[31:0] = in_8; b22[31:0] = in_9; flag = in_1
endmodule

module \初始化a  (
  input  in_1,
  input  [31:0] in_2,
  input  [31:0] in_3,
  input  [31:0] in_4,
  input  [31:0] in_5,
  output [31:0] out_6,
  output [31:0] out_7,
  output [31:0] out_8,
  output [31:0] out_9
);

  Multiplexer #(.width(32)) multiplexer_1 (.in0(32'h1), .in1(in_2), .out(out_6), .sel(in_1));  // open: en
  Multiplexer #(.width(32)) multiplexer_2 (.in0(32'h1), .in1(in_3), .out(out_7), .sel(in_1));  // open: en
  Multiplexer #(.width(32)) multiplexer_3 (.in0(32'h1), .in1(in_4), .out(out_8), .sel(in_1));  // open: en
  Multiplexer #(.width(32)) multiplexer_4 (.in0({32{1'b0}}), .in1(in_5), .out(out_9), .sel(in_1));  // open: en

  // Other names for the same wires on the sheet: t = in_1
endmodule

module \初始化s  (
  input  in_1,
  input  [31:0] in_2,
  input  [31:0] in_3,
  input  [31:0] in_4,
  input  [31:0] in_5,
  output [31:0] out_6,
  output [31:0] out_7,
  output [31:0] out_8,
  output [31:0] out_9
);

  Multiplexer #(.width(32)) multiplexer_1 (.in0(32'h1), .in1(in_2), .out(out_6), .sel(in_1));  // open: en
  Multiplexer #(.width(32)) multiplexer_2 (.in0({32{1'b0}}), .in1(in_3), .out(out_7), .sel(in_1));  // open: en
  Multiplexer #(.width(32)) multiplexer_3 (.in0(32'h1), .in1(in_4), .out(out_8), .sel(in_1));  // open: en
  Multiplexer #(.width(32)) multiplexer_4 (.in0({32{1'b0}}), .in1(in_5), .out(out_9), .sel(in_1));  // open: en

  // Other names for the same wires on the sheet: t = in_1
endmodule

module try (
  input  [31:0] in_1
);

  wire clock_1_out;

  Clock clock_1 (.out(clock_1_out));
  Counter counter_1 (.clk(clock_1_out));  // open: load, D, count, Q, carry, clr
  Register #(.width(32)) register_1 (.D(in_1));  // open: en, Q, clk, clr
endmodule

module main_new (
  input  [31:0] in_1,
  output [31:0] out_2
);

  wire and_1_out, clk, low, stop, t;
  wire [31:0] a11, a12, a21, a22, multiplexer_1_out, n, register_1_q, register_2_q, s11, s12, s21, s22,
       \初始化a_1_out_6 , \初始化a_1_out_7 , \初始化a_1_out_8 , \初始化a_1_out_9 , \初始化s_1_out_6 , \初始化s_1_out_7 ,
       \初始化s_1_out_8 , \初始化s_1_out_9 , \矩阵乘法_1_out_10 , \矩阵乘法_1_out_11 , \矩阵乘法_1_out_12 , \矩阵乘法_1_out_13 ,
       \矩阵乘法_2_out_10 , \矩阵乘法_2_out_11 , \矩阵乘法_2_out_12 , \矩阵乘法_2_out_13 ;

  Clock clock_1 (.out(clk));
  Counter #(.width(1), .max('h1), .ongoal("stay")) counter_1 (.Q(t), .clk(clk));  // open: load, D, count, carry, clr
  Register #(.width(32)) register_1 (.D(multiplexer_1_out), .Q(register_1_q), .clk(clk));  // open: en, clr
  Multiplexer #(.width(32)) multiplexer_1 (.in0(in_1), .in1(n), .out(multiplexer_1_out), .sel(t));  // open: en
  \初始化a  \u_初始化a_1  (
    .in_1(t), .in_2(a11), .in_3(a12), .in_4(a21), .in_5(a22), .out_6(\初始化a_1_out_6 ), .out_7(\初始化a_1_out_7 ),
    .out_8(\初始化a_1_out_8 ), .out_9(\初始化a_1_out_9 ));
  \矩阵乘法  \u_矩阵乘法_1  (
    .in_2(\初始化a_1_out_6 ), .in_3(\初始化a_1_out_7 ), .in_4(\初始化a_1_out_8 ), .in_5(\初始化a_1_out_9 ), .in_6(a11),
    .in_7(a12), .in_8(a21), .in_9(a22), .out_10(\矩阵乘法_1_out_10 ), .in_1(t), .out_11(\矩阵乘法_1_out_11 ),
    .out_12(\矩阵乘法_1_out_12 ), .out_13(\矩阵乘法_1_out_13 ));
  Shifter #(.width(32), .shift("lr")) shifter_1 (.in(register_1_q), .\dist (5'b00001), .out(n));
  Bit_Extender #(.in_width(32), .out_width(1)) bit_extender_1 (.in(register_1_q), .out(low));
  Comparator #(.width(32), .mode("unsigned")) comparator_1 (
    .a(register_1_q), .b({32{1'b0}}), .gt(stop));  // open: eq, lt
  rgt rgt_1 (
    .in_1(\矩阵乘法_1_out_10 ), .in_2(\矩阵乘法_1_out_11 ), .in_3(\矩阵乘法_1_out_12 ), .in_4(\矩阵乘法_1_out_13 ),
    .out_8(a11), .out_9(a12), .out_10(a21), .out_11(a22), .in_5(clk), .in_7(1'b1));  // open: in_6
  Register #(.width(32)) register_2 (.D(s12), .Q(register_2_q), .clk(clk), .clr(stop));  // open: en
  Multiplexer #(.width(32)) multiplexer_2 (.in0(register_2_q), .in1({32{1'b0}}), .out(out_2), .sel(stop));  // open: en
  \初始化s  \u_初始化s_1  (
    .in_1(t), .in_2(s11), .in_3(s12), .in_4(s21), .in_5(s22), .out_6(\初始化s_1_out_6 ), .out_7(\初始化s_1_out_7 ),
    .out_8(\初始化s_1_out_8 ), .out_9(\初始化s_1_out_9 ));
  \矩阵乘法  \u_矩阵乘法_2  (
    .in_2(\初始化s_1_out_6 ), .in_3(\初始化s_1_out_7 ), .in_4(\初始化s_1_out_8 ), .in_5(\初始化s_1_out_9 ), .in_6(a11),
    .in_7(a12), .in_8(a21), .in_9(a22), .out_10(\矩阵乘法_2_out_10 ), .in_1(and_1_out), .out_11(\矩阵乘法_2_out_11 ),
    .out_12(\矩阵乘法_2_out_12 ), .out_13(\矩阵乘法_2_out_13 ));
  and and_1 (and_1_out, t, low);
  rgt rgt_2 (
    .in_1(\矩阵乘法_2_out_10 ), .in_2(\矩阵乘法_2_out_11 ), .in_3(\矩阵乘法_2_out_12 ), .in_4(\矩阵乘法_2_out_13 ),
    .out_8(s11), .out_9(s12), .out_10(s21), .out_11(s22), .in_5(clk), .in_7(1'b1));  // open: in_6
endmodule
