// Logisim project mod5.circ as structural Verilog: 3 circuits, main circuit mod5
module mod5 (
  input  in_1,
  output out_2,
  output out_3,
  output out_4,
  output out_5,
  output out_6
);

  wire clock_1_out;
  wire [1:0] move_1_c0_, register_1_q;

  move move_1 (.C1(register_1_q[1]), .C0(register_1_q[0]), .b(in_1), .C1_(move_1_c0_[1]), .C0_(move_1_c0_[0]));
  Clock clock_1 (.out(clock_1_out));
  Register #(.width(2)) register_1 (.D(move_1_c0_), .Q(register_1_q), .clk(clock_1_out));  // open: en, clr
  out out_1 (
    .b(in_1), .S0(out_2), .S1(out_3), .S2(out_4), .S3(out_5), .S4(out_6), .C1(register_1_q[1]),
    .C0(register_1_q[0]));
endmodule

module move (
  input  C1,
  input  C0,
  input  b,
  output C1_,
  output C0_
);

  wire and_1_out, and_2_out, and_3_out, and_4_out, and_5_out, and_6_out, and_7_out, and_8_out, and_9_out,
       and_10_out, not_1_out, not_2_out, not_3_out, not_4_out, not_5_out, not_6_out, not_7_out, not_8_out,
       or_2_out, or_3_out;

  not not_1 (not_1_out, C1);
  not not_2 (not_2_out, C0);
  not not_3 (not_3_out, C1);
  not not_4 (not_4_out, C0);
  not not_5 (not_5_out, C1);
  not not_6 (not_6_out, C0);
  and and_1 (and_1_out, not_1_out, C0);
  and and_2 (and_2_out, C1, not_2_out);
  and and_3 (and_3_out, not_3_out, not_4_out);
  and and_4 (and_4_out, not_5_out, C0);
  not not_7 (not_7_out, b);
  and and_5 (and_5_out, C1, not_6_out);
  not not_8 (not_8_out, b);
  and and_6 (and_6_out, C1, C0);
  or or_1 (C1_, and_1_out, and_2_out);
  and and_7 (and_7_out, and_3_out, b);
  and and_8 (and_8_out, and_4_out, not_7_out);
  and and_9 (and_9_out, and_5_out, not_8_out);
  and and_10 (and_10_out, and_6_out, b);
  or or_2 (or_2_out, and_7_out, and_8_out);
  or or_3 (or_3_out, and_9_out, and_10_out);
  or or_4 (C0_, or_2_out, or_3_out);
endmodule

module out (
  input  C1,
  input  C0,
  input  b,
  output S0,
  output S1,
  output S2,
  output S3,
  output S4
);

  wire and_1_out, and_2_out, and_3_out, and_4_out, and_5_out, and_6_out, and_7_out, and_8_out, and_9_out,
       and_10_out, and_11_out, and_12_out, and_13_out, and_14_out, and_15_out, and_16_out, not_1_out,
       not_2_out, not_3_out, not_4_out, not_5_out, not_6_out, not_7_out, not_8_out, not_9_out, not_10_out,
       not_11_out, not_12_out;

  not not_1 (not_1_out, C1);
  not not_2 (not_2_out, C0);
  not not_3 (not_3_out, C1);
  not not_4 (not_4_out, C0);
  not not_5 (not_5_out, C1);
  not not_6 (not_6_out, C0);
  not not_7 (not_7_out, C1);
  not not_8 (not_8_out, C0);
  and and_1 (and_1_out, not_1_out, not_2_out);
  not not_9 (not_9_out, b);
  and and_2 (and_2_out, C1, C0);
  not not_10 (not_10_out, b);
  and and_3 (and_3_out, not_3_out, not_4_out);
  and and_4 (and_4_out, C1, C0);
  and and_5 (and_5_out, not_5_out, C0);
  and and_6 (and_6_out, C1, not_6_out);
  and and_7 (and_7_out, not_7_out, C0);
  not not_11 (not_11_out, b);
  and and_8 (and_8_out, C1, not_8_out);
  not not_12 (not_12_out, b);
  and and_9 (and_9_out, and_1_out, not_9_out);
  and and_10 (and_10_out, and_2_out, not_10_out);
  and and_11 (and_11_out, and_3_out, b);
  and and_12 (and_12_out, and_4_out, b);
  and and_13 (and_13_out, and_5_out, b);
  and and_14 (and_14_out, and_6_out, b);
  and and_15 (and_15_out, and_7_out, not_11_out);
  and and_16 (and_16_out, and_8_out, not_12_out);
  or or_1 (S1, and_9_out, and_10_out);
  or or_2 (S2, and_11_out, and_12_out);
  or or_3 (S3, and_13_out, and_14_out);
  or or_4 (S4, and_15_out, and_16_out);

  assign S0 = 1'b0;
endmodule
